# Fritzing sketch custom_circuit_project_file (saved by Fritzing 0.7.4b)
breadboards: 1

parts:
  Arduino1 = Arduino
  1M_R = Resistor [tolerance=±5% resistance=1M package=THT]
  R1 = Resistor [tolerance=±5% resistance=220 package=THT]

nets:
  N1: Arduino1.GND, 1M_R.Pin_0, R1.Pin_0
  N2: Arduino1.A2, 1M_R.Pin_1
  N3: Arduino1.A5, R1.Pin_1

notes:
  1. 5V
  PING
  Sharp
  2. 5V
  3. 5V
  4. 5V
  +
  -
  Sag Agirlik
  Sol Agirlik
  IT'S A CRANK CHAIR
  Burcu Celiksap
